// Logisim project BCD_catodo.circ as structural Verilog: 1 circuit, main circuit main
module main (
  input  A,
  input  B,
  input  C,
  input  D
);

  wire and_1_out, and_2_out, and_3_out, and_4_out, and_5_out, and_6_out, and_7_out, and_8_out, and_9_out,
       and_10_out, and_11_out, and_12_out, and_13_out, and_14_out, and_15_out, and_16_out, and_17_out,
       and_18_out, and_19_out, and_20_out, and_21_out, and_22_out, and_23_out, and_24_out, and_25_out,
       and_26_out, and_27_out, or_1_out, or_2_out, or_3_out, or_4_out, or_5_out, or_6_out, or_7_out;

  and and_1 (and_1_out, ~A, C);  // AND_Gate
  and and_2 (and_2_out, A, ~B, ~C);  // AND_Gate
  and and_3 (and_3_out, ~B, ~C, ~D);  // AND_Gate
  and and_4 (and_4_out, ~A, B, D);  // AND_Gate
  and and_5 (and_5_out, ~A, ~B);  // AND_Gate
  and and_6 (and_6_out, ~B, ~C);  // AND_Gate
  and and_7 (and_7_out, ~A, ~C, ~D);  // AND_Gate
  and and_8 (and_8_out, ~A, C, D);  // AND_Gate
  and and_9 (and_9_out, ~A, B);  // AND_Gate
  and and_10 (and_10_out, ~A, ~C);  // AND_Gate
  and and_11 (and_11_out, ~A, D);  // AND_Gate
  and and_12 (and_12_out, ~B, ~C);  // AND_Gate
  and and_13 (and_13_out, A, ~B, ~C);  // AND_Gate
  and and_14 (and_14_out, ~A, C, ~D);  // AND_Gate
  and and_15 (and_15_out, ~A, ~B, C);  // AND_Gate
  and and_16 (and_16_out, ~B, ~C, ~D);  // AND_Gate
  and and_17 (and_17_out, ~A, B, ~C, D);  // AND_Gate
  and and_18 (and_18_out, ~A, C, ~D);  // AND_Gate
  and and_19 (and_19_out, ~B, ~C, ~D);  // AND_Gate
  and and_20 (and_20_out, A, ~B, ~C);  // AND_Gate
  and and_21 (and_21_out, ~A, B, ~C);  // AND_Gate
  and and_22 (and_22_out, ~B, ~C, ~D);  // AND_Gate
  and and_23 (and_23_out, ~A, B, ~D);  // AND_Gate
  and and_24 (and_24_out, A, ~B, ~C);  // AND_Gate
  and and_25 (and_25_out, ~A, ~B, C);  // AND_Gate
  and and_26 (and_26_out, ~A, B, ~C);  // AND_Gate
  and and_27 (and_27_out, ~A, C, ~D);  // AND_Gate
  or or_1 (or_1_out, and_1_out, and_2_out, and_3_out, and_4_out);
  or or_2 (or_2_out, and_5_out, and_6_out, and_7_out, and_8_out);
  or or_3 (or_3_out, and_9_out, and_10_out, and_11_out, and_12_out);
  or or_4 (or_4_out, and_13_out, and_14_out, and_15_out, and_16_out, and_17_out);
  or or_5 (or_5_out, and_18_out, and_19_out);
  or or_6 (or_6_out, and_20_out, and_21_out, and_22_out, and_23_out);
  or or_7 (or_7_out, and_24_out, and_25_out, and_26_out, and_27_out);
  _7_Segment_Display u_7_segment_display_1 (
    .g(or_7_out), .f(or_6_out), .a(or_1_out), .b(or_2_out), .e(or_5_out), .d(or_4_out), .c(or_3_out));  // open: dp
endmodule
