// Logisim project BCD_errado.circ as structural Verilog: 1 circuit, main circuit main
module main (
  input  A,
  input  B,
  input  C,
  input  D
);

  wire and_1_out, and_2_out, and_3_out, and_4_out, and_5_out, and_6_out, and_7_out, and_8_out, and_9_out,
       and_10_out, and_11_out, and_12_out, and_13_out, and_14_out, and_15_out, and_16_out, and_17_out,
       or_1_out, or_2_out, or_3_out, or_4_out, or_5_out, or_6_out, or_7_out, or_8_out, or_9_out, or_10_out,
       or_11_out, or_12_out, or_13_out, xnor_1_out, xor_1_out, xor_2_out;

  or or_1 (or_1_out, C, D);
  xor xor_1 (xor_1_out, B, D);
  xor xor_2 (xor_2_out, C, D);
  or or_2 (or_2_out, B, C, D);
  or or_3 (or_3_out, B, C);
  xnor xnor_1 (xnor_1_out, C, D);
  or or_4 (or_4_out, B, C);
  and and_1 (and_1_out, or_1_out, A);
  and and_2 (and_2_out, ~C, xor_1_out);  // AND_Gate
  and and_3 (and_3_out, or_2_out, A);
  and and_4 (and_4_out, or_3_out, A);
  and and_5 (and_5_out, xnor_1_out, B);
  and and_6 (and_6_out, ~A, ~B, ~C, D);  // AND_Gate
  and and_7 (and_7_out, A, C);
  and and_8 (and_8_out, B, ~C);  // AND_Gate
  or or_5 (or_5_out, A, ~B, D);  // OR_Gate
  and and_9 (and_9_out, or_4_out, A);
  and and_10 (and_10_out, ~A, ~B, ~C);  // AND_Gate
  and and_11 (and_11_out, B, C, D);
  or or_6 (or_6_out, B, C, D);
  or or_7 (or_7_out, and_1_out, and_2_out);
  and and_12 (and_12_out, B, xor_2_out);
  or or_8 (or_8_out, and_4_out, and_5_out, and_6_out);
  and and_13 (and_13_out, A, B);
  and and_14 (and_14_out, or_5_out, C);
  and and_15 (and_15_out, ~A, ~B, D);  // AND_Gate
  and and_16 (and_16_out, or_6_out, A);
  and and_17 (and_17_out, ~B, C, ~D);  // AND_Gate
  or or_9 (or_9_out, and_12_out, and_3_out);
  or or_10 (or_10_out, and_7_out, and_8_out, D);
  or or_11 (or_11_out, and_13_out, and_14_out, and_15_out);
  or or_12 (or_12_out, and_9_out, and_10_out, and_11_out);
  _7_Segment_Display #(.active("false")) u_7_segment_display_1 (
    .g(or_12_out), .f(or_11_out), .a(or_7_out), .b(or_9_out), .e(or_10_out), .d(or_8_out), .c(or_13_out));  // open: dp
  or or_13 (or_13_out, and_16_out, and_17_out);
endmodule
