// Logisim project PROJETO1.circ as structural Verilog: 2 circuits, main circuit main
module main (
  input  A,
  input  B,
  input  C,
  input  D,
  output a_2,
  output b_2,
  output c_2,
  output d_2,
  output e,
  output f,
  output g
);

  wire and_1_out, and_2_out, and_3_out, and_4_out, and_5_out, and_6_out, and_7_out, and_8_out, and_9_out,
       and_10_out, and_11_out, and_12_out, and_13_out, and_14_out, and_15_out, and_16_out, and_17_out,
       and_18_out, and_19_out, and_20_out, and_21_out, and_22_out, and_23_out, and_24_out, and_25_out,
       and_26_out, and_27_out;

  and and_1 (and_1_out, ~A, C);  // AND_Gate
  and and_2 (and_2_out, A, ~B, ~C);  // AND_Gate
  and and_3 (and_3_out, ~B, ~C, ~D);  // AND_Gate
  and and_4 (and_4_out, ~A, B, D);  // AND_Gate
  and and_5 (and_5_out, ~A, ~B);  // AND_Gate
  and and_6 (and_6_out, ~B, ~C);  // AND_Gate
  and and_7 (and_7_out, ~A, ~C, ~D);  // AND_Gate
  and and_8 (and_8_out, ~A, C, D);  // AND_Gate
  and and_9 (and_9_out, ~A, B);  // AND_Gate
  and and_10 (and_10_out, ~A, ~C);  // AND_Gate
  and and_11 (and_11_out, ~A, D);  // AND_Gate
  and and_12 (and_12_out, ~B, ~C);  // AND_Gate
  and and_13 (and_13_out, A, ~B, ~C);  // AND_Gate
  and and_14 (and_14_out, ~A, C, ~D);  // AND_Gate
  and and_15 (and_15_out, ~A, ~B, C);  // AND_Gate
  and and_16 (and_16_out, ~B, ~C, ~D);  // AND_Gate
  and and_17 (and_17_out, ~A, B, ~C, D);  // AND_Gate
  and and_18 (and_18_out, ~A, C, ~D);  // AND_Gate
  and and_19 (and_19_out, ~B, ~C, ~D);  // AND_Gate
  and and_20 (and_20_out, A, ~B, ~C);  // AND_Gate
  and and_21 (and_21_out, ~A, B, ~C);  // AND_Gate
  and and_22 (and_22_out, ~B, ~C, ~D);  // AND_Gate
  and and_23 (and_23_out, ~A, B, ~D);  // AND_Gate
  and and_24 (and_24_out, A, ~B, ~C);  // AND_Gate
  and and_25 (and_25_out, ~A, ~B, C);  // AND_Gate
  and and_26 (and_26_out, ~A, B, ~C);  // AND_Gate
  and and_27 (and_27_out, ~A, C, ~D);  // AND_Gate
  or or_1 (a_2, and_1_out, and_2_out, and_3_out, and_4_out);
  or or_2 (b_2, and_5_out, and_6_out, and_7_out, and_8_out);
  or or_3 (c_2, and_9_out, and_10_out, and_11_out, and_12_out);
  or or_4 (d_2, and_13_out, and_14_out, and_15_out, and_16_out, and_17_out);
  or or_5 (e, and_18_out, and_19_out);
  or or_6 (f, and_20_out, and_21_out, and_22_out, and_23_out);
  or or_7 (g, and_24_out, and_25_out, and_26_out, and_27_out);
endmodule

module BCD_catode (
  input  A,
  input  B,
  input  C,
  input  D
);

  wire main_1_a_2, main_1_b_2, main_1_c_2, main_1_d_2, main_1_e, main_1_f, main_1_g;

  main main_1 (
    .A(A), .B(B), .C(C), .D(D), .a_2(main_1_a_2), .b_2(main_1_b_2), .c_2(main_1_c_2), .d_2(main_1_d_2),
    .e(main_1_e), .f(main_1_f), .g(main_1_g));
  _7_Segment_Display u_7_segment_display_1 (
    .g(main_1_g), .f(main_1_f), .a(main_1_a_2), .b(main_1_b_2), .e(main_1_e), .d(main_1_d_2), .c(main_1_c_2));  // open: dp
endmodule
